# Fritzing sketch kvm_remote (saved by Fritzing 0.9.9b)
perfboards: 1

parts:
  MH-ET_LIVE_ESP32_DEVKIT1 = MH-ET LIVE ESP32 DEVKIT 38 pins
  D1 = LTE-302 [package=lte-302]
  LED1 = smd LED [color="Red (633nm)" package="1206 [SMD]"]
  S1 = Momentary Switch [package=ksa_sealed_tac_switch]
  S2 = Momentary Switch [package=ksa_sealed_tac_switch]
  VCC1 = Battery block 9V
  R1 = Resistor [tolerance=±5% resistance=1k package=THT]
  R2 = Resistor [tolerance=±5% resistance=1k power=0.25 package=THT]

nets:
  N1: MH-ET_LIVE_ESP32_DEVKIT1.3V3, S1.3, S2.1
  N2: MH-ET_LIVE_ESP32_DEVKIT1.IO34, S2.4, R2.Pin_0
  N3: MH-ET_LIVE_ESP32_DEVKIT1.IO35, S1.2, R1.Pin_0
  N4: MH-ET_LIVE_ESP32_DEVKIT1.GND#58, VCC1.-, R2.Pin_1
  N5: MH-ET_LIVE_ESP32_DEVKIT1.5V, VCC1.+
  N6: MH-ET_LIVE_ESP32_DEVKIT1.GND#64, D1.C, LED1.cathode, R1.Pin_1
  N7: MH-ET_LIVE_ESP32_DEVKIT1.IO4, D1.A
  N8: MH-ET_LIVE_ESP32_DEVKIT1.IO0, LED1.anode

custom parts:
  MH-ET LIVE ESP32 DEVKIT 38 pins: http://mh.nodebb.com/topic/2/mh-et-live-esp32-devkit
